// Logisim project RISC_V_CPU.circ as structural Verilog: 5 circuits, main circuit CPU
module CPU (
);

  wire [9:0] program_counter_1_out_5;

  Program_Counter program_counter_1 (.out_5(program_counter_1_out_5));  // open: in_2, in_3, in_4, in_1
  Instruction_Memory instruction_memory_1 (.in_1(program_counter_1_out_5));  // open: out_2
endmodule

module Program_Counter (
  input  [9:0] in_1,
  input  in_2,
  input  in_3,
  input  in_4,
  output [9:0] out_5
);

  Counter #(.max('h3ff), .width(10)) counter_1 (
    .clr(in_2), .load(in_3), .clk(in_4), .D(in_1), .Q(out_5));  // open: up, count, carry

  // Other names for the same wires on the sheet: ADDR_IN[9:0] = in_1; ADDR_OUT[9:0] = out_5
endmodule

module Instruction_Memory (
  input  [9:0] in_1,
  output [31:0] out_2
);

  ROM #(.addrWidth(10), .dataWidth(32)) rom_1 (.addr(in_1), .data(out_2));

  // Other names for the same wires on the sheet: ADDR_IN[9:0] = in_1; ADDR_OUT[31:0] = out_2
endmodule

module Instruction_Decoder (
  input  [31:0] in_1,
  input  [6:0] in_2,
  input  in_3,
  input  in_4
);

  wire and_5_out, and_6_out, and_7_out, and_8_out, and_9_out, and_10_out, b_type, clk, i_type, imm_valid,
       j_type, or_3_out, or_4_out, r_type, rd_valid, rs1_valid, rs2_valid, s_type, u_type;
  wire [2:0] funct3;
  wire [4:0] i_imm;
  wire [6:6] funct7;
  wire [12:1] b_imm;
  wire [20:16] j_imm;

  Register #(.width(32)) Instruction_Register (
    .D(in_1), .clk(clk), .Q({funct7[6], b_imm[10:5], i_imm, j_imm, funct3, b_imm[4:1], b_imm[12], in_2}));  // open: en, clr
  Clock clock_1 (.out(clk));
  and and_1 (u_type, ~in_2[6], in_2[4], ~in_2[3], in_2[2]);  // AND_Gate
  and and_2 (b_type, in_2[6], in_2[5], ~in_2[4], ~in_2[3], ~in_2[2]);  // AND_Gate
  and and_3 (s_type, ~in_2[6], in_2[5], ~in_2[4], ~in_2[3]);  // AND_Gate
  and and_4 (j_type, in_2[6], in_2[5], ~in_2[4], in_2[3], in_2[2]);  // AND_Gate
  and and_5 (and_5_out, ~in_2[6], in_2[5]);  // AND_Gate
  and and_6 (and_6_out, in_2[6], ~in_2[5], in_2[4], ~in_2[3], ~in_2[2]);  // AND_Gate
  and and_7 (and_7_out, ~in_2[6], ~in_2[5], ~in_2[4], ~in_2[3]);  // AND_Gate
  and and_8 (and_8_out, ~in_2[6], ~in_2[5], in_2[4], ~in_2[2]);  // AND_Gate
  and and_9 (and_9_out, in_2[6], in_2[5], ~in_2[4], ~in_2[3], in_2[2]);  // AND_Gate
  and and_10 (and_10_out, ~in_2[6], ~b_imm[12], ~b_imm[1], ~b_imm[2], ~b_imm[3]);  // AND_Gate
  or or_1 (r_type, and_5_out, and_6_out);
  or or_2 (i_type, and_7_out, and_8_out, and_9_out);
  or or_3 (or_3_out, b_type, and_10_out, s_type);
  or or_4 (or_4_out, j_type, u_type);
  or or_5 (rs2_valid, r_type, s_type, b_type);
  not not_1 (rd_valid, or_3_out);
  not not_2 (imm_valid, r_type);
  not not_3 (rs1_valid, or_4_out);

  // Other names for the same wires on the sheet: ADDR_IN[31:0] = in_1; b_imm (some bits) = {b_imm[12], in_3};
  //   j_imm[15:0] = {funct3, {2{i_imm[0]}}, b_imm[9:5], i_imm, in_4};
  //   u_imm[19:0] = {funct7[6], b_imm[10:5], i_imm, j_imm, funct3}; funct7[5:0] = b_imm[10:5];
  //   i_imm[11:5] = {funct7[6], b_imm[10:5]}; s_imm[11:0] = {funct7[6], b_imm[10:1], b_imm[12]}; op[6:0] = in_2;
  //   rd[4:0] = {b_imm[4:1], b_imm[12]}; rs1[4:0] = j_imm; rs2[4:0] = i_imm

  // Notes on the sheet:
  //   Instruction Decoder
  //   Control Unit
  //   Validation of fields
  //   Instruction types
endmodule

module Arithmetic (
  input  [31:0] a,
  input  [31:0] b,
  output [31:0] y
);

  wire comparator_1_eq, comparator_1_gt, comparator_1_lt, not_1_out, or_1_out;

  Comparator #(.width(32)) comparator_1 (
    .a(a), .b(b), .gt(comparator_1_gt), .eq(comparator_1_eq), .lt(comparator_1_lt));
  Adder #(.width(32)) adder_1 (.a(a), .b(b), .out(y));  // open: cin, cout
  not not_1 (not_1_out, comparator_1_eq);
  or or_1 (or_1_out, comparator_1_gt, comparator_1_eq);
endmodule
